// Logisim project solutions.circ as structural Verilog: 15 circuits, main circuit Rise/fall detector 1
module NOT (
  input  A,
  output Q
);

  Transistor transistor_1 (.in(1'b1), .out(Q), .gate(A));
  Transistor #(.\type ("n")) transistor_2 (.in(1'b0), .out(Q), .gate(A));
endmodule

module NOR (
  input  A,
  input  B,
  output Q
);

  wire transistor_1_out;

  Transistor transistor_1 (.in(1'b1), .out(transistor_1_out), .gate(A));
  Transistor transistor_2 (.in(transistor_1_out), .out(Q), .gate(B));
  Transistor #(.\type ("n")) transistor_3 (.in(1'b0), .out(Q), .gate(A));
  Transistor #(.\type ("n")) transistor_4 (.in(1'b0), .out(Q), .gate(B));
endmodule

module NAND (
  input  A,
  input  B,
  output Q
);

  wire transistor_3_out;

  Transistor transistor_1 (.in(1'b1), .out(Q), .gate(A));
  Transistor #(.\type ("n")) transistor_2 (.in(transistor_3_out), .out(Q), .gate(A));
  Transistor #(.\type ("n")) transistor_3 (.in(1'b0), .out(transistor_3_out), .gate(B));
  Transistor transistor_4 (.in(1'b1), .out(Q), .gate(B));
endmodule

module OR (
  input  A,
  input  B,
  output Q
);

  wire transistor_1_out, transistor_2_out;

  Transistor transistor_1 (.in(1'b1), .out(transistor_1_out), .gate(A));
  Transistor transistor_2 (.in(transistor_1_out), .out(transistor_2_out), .gate(B));
  Transistor #(.\type ("n")) transistor_3 (.in(1'b0), .out(transistor_2_out), .gate(A));
  Transistor #(.\type ("n")) transistor_4 (.in(1'b0), .out(transistor_2_out), .gate(B));
  Transistor transistor_5 (.in(1'b1), .out(Q), .gate(transistor_2_out));
  Transistor #(.\type ("n")) transistor_6 (.in(1'b0), .out(Q), .gate(transistor_2_out));
endmodule

module AND (
  input  A,
  input  B,
  output Q
);

  wire transistor_1_out, transistor_3_out;

  Transistor transistor_1 (.in(1'b1), .out(transistor_1_out), .gate(A));
  Transistor #(.\type ("n")) transistor_2 (.in(transistor_3_out), .out(transistor_1_out), .gate(A));
  Transistor #(.\type ("n")) transistor_3 (.in(1'b0), .out(transistor_3_out), .gate(B));
  Transistor transistor_4 (.in(1'b1), .out(transistor_1_out), .gate(B));
  Transistor transistor_5 (.in(1'b1), .out(Q), .gate(transistor_1_out));
  Transistor #(.\type ("n")) transistor_6 (.in(1'b0), .out(Q), .gate(transistor_1_out));
endmodule

module One_shot (
  input  in,
  input  in_2,
  output out,
  output out_2
);

  wire and_1_out, clock_1_out, d_ff_1_q, not_1_out;

  not not_1 (not_1_out, d_ff_1_q);
  and and_1 (and_1_out, not_1_out, in);
  Clock clock_1 (.out(clock_1_out));
  D_Flip_Flop d_ff_1 (.clk(clock_1_out), .D(in), .Q(d_ff_1_q));  // open: Qn, preset, en, reset
  D_Flip_Flop d_ff_2 (.clk(clock_1_out), .D(and_1_out), .Q(out));  // open: Qn, preset, en, reset

  // Notes on the sheet:
  //   Logic
  //   Storage
  //   State
  //   Output
endmodule

module Rise_fall_detector_1 (
  input  in,
  output rise,
  output fall
);

  wire not_1_out;

  not not_1 (not_1_out, in);
  One_shot one_shot_1 (.in(in), .out(rise));  // open: out_2, in_2
  One_shot one_shot_2 (.in(not_1_out), .out(fall));  // open: out_2, in_2
endmodule

module Rise_fall_detector_2 (
  input  in,
  input  in_2,
  output rise,
  output fall,
  output rise_2,
  output fall_2
);

  wire and_1_out, and_2_out, clock_1_out, clock_2_out, d_ff_1_q, d_ff_1_qn, d_ff_2_q, d_ff_2_qn, d_ff_3_q,
       d_ff_3_qn, not_1_out;

  Clock clock_1 (.out(clock_1_out));
  D_Flip_Flop d_ff_1 (.clk(clock_1_out), .D(in), .Q(d_ff_1_q), .Qn(d_ff_1_qn));  // open: preset, en, reset
  D_Flip_Flop d_ff_2 (.clk(clock_1_out), .D(d_ff_1_q), .Q(d_ff_2_q), .Qn(d_ff_2_qn));  // open: preset, en, reset
  and and_1 (and_1_out, d_ff_3_qn, in_2);
  and and_2 (and_2_out, d_ff_3_q, not_1_out);
  not not_1 (not_1_out, in_2);
  and and_3 (rise, d_ff_1_q, d_ff_2_qn);
  and and_4 (fall, d_ff_1_qn, d_ff_2_q);
  Clock clock_2 (.out(clock_2_out));
  D_Flip_Flop d_ff_3 (.clk(clock_2_out), .D(in_2), .Q(d_ff_3_q), .Qn(d_ff_3_qn));  // open: preset, en, reset
  D_Flip_Flop d_ff_4 (.clk(clock_2_out), .D(and_1_out), .Q(rise_2));  // open: Qn, preset, en, reset
  D_Flip_Flop d_ff_5 (.clk(clock_2_out), .D(and_2_out), .Q(fall_2));  // open: Qn, preset, en, reset
endmodule

module Program_counter (
  input  [15:0] in,
  input  reset,
  input  inc,
  input  load,
  output [15:0] out
);

  wire clock_1_out, or_1_out;
  wire [15:0] adder_1_out, multiplexer_1_out, multiplexer_2_out;

  Multiplexer #(.width(16), .enable("false")) multiplexer_1 (
    .in0({16{1'b0}}), .in1(adder_1_out), .out(multiplexer_1_out), .sel(inc));
  Multiplexer #(.width(16), .enable("false")) multiplexer_2 (
    .in0(multiplexer_1_out), .in1(in), .out(multiplexer_2_out), .sel(load));
  or or_1 (or_1_out, reset, inc, load);
  Register #(.width(16)) register_1 (.D(multiplexer_2_out), .en(or_1_out), .Q(out), .clk(clock_1_out));  // open: clr
  Clock clock_1 (.out(clock_1_out));
  Adder #(.width(16)) adder_1 (.a(16'h1), .b(out), .out(adder_1_out));  // open: cin, cout
endmodule

module Brain (
  input  change,
  output green,
  output amber,
  output red,
  output flash_amber
);

  wire clock_1_out, multiplexer_1_out, multiplexer_2_out, multiplexer_3_out, multiplexer_4_out,
       one_shot_1_out, or_1_out;

  One_shot one_shot_1 (.in(1'b1), .out(one_shot_1_out));  // open: out_2, in_2
  or or_1 (or_1_out, green, one_shot_1_out);
  Multiplexer #(.enable("false")) multiplexer_1 (
    .in0(or_1_out), .in1(flash_amber), .out(multiplexer_1_out), .sel(change));
  Multiplexer #(.enable("false")) multiplexer_2 (.in0(amber), .in1(green), .out(multiplexer_2_out), .sel(change));
  Multiplexer #(.enable("false")) multiplexer_3 (.in0(red), .in1(amber), .out(multiplexer_3_out), .sel(change));
  Multiplexer #(.enable("false")) multiplexer_4 (.in0(flash_amber), .in1(red), .out(multiplexer_4_out), .sel(change));
  Clock clock_1 (.out(clock_1_out));
  D_Flip_Flop d_ff_1 (.clk(clock_1_out), .D(multiplexer_1_out), .Q(green));  // open: Qn, preset, en, reset
  D_Flip_Flop d_ff_2 (.clk(clock_1_out), .D(multiplexer_2_out), .Q(amber));  // open: Qn, preset, en, reset
  D_Flip_Flop d_ff_3 (.clk(clock_1_out), .D(multiplexer_3_out), .Q(red));  // open: Qn, preset, en, reset
  D_Flip_Flop d_ff_4 (.clk(clock_1_out), .D(multiplexer_4_out), .Q(flash_amber));  // open: Qn, preset, en, reset
endmodule

module Equal (
  input  [15:0] x,
  input  [15:0] y,
  output out
);

  wire [15:0] not_1_out, xor_1_out;

  assign xor_1_out = x ^ y;  // XOR_Gate xor_1, 16 bits wide
  assign not_1_out = ~xor_1_out;  // NOT_Gate not_1, 16 bits wide
  and and_1 (out, not_1_out[0], not_1_out[1], not_1_out[2], not_1_out[3], not_1_out[4], not_1_out[5], not_1_out[6], not_1_out[7], not_1_out[8], not_1_out[9], not_1_out[10], not_1_out[11], not_1_out[12], not_1_out[13], not_1_out[14], not_1_out[15]);
endmodule

module Timer (
  input  [15:0] \time ,
  input  in,
  output done
);

  wire and_1_out, and_2_out, clock_1_out, clock_2_out, d_ff_1_qn, not_1_out, not_2_out, or_1_out;
  wire [15:0] counter_1_q;

  Clock clock_1 (.out(clock_1_out));
  D_Flip_Flop d_ff_1 (.clk(clock_1_out), .D(in), .Qn(d_ff_1_qn));  // open: Q, preset, en, reset
  and and_1 (and_1_out, d_ff_1_qn, in);
  not not_1 (not_1_out, in);
  not not_2 (not_2_out, done);
  or or_1 (or_1_out, and_1_out, not_1_out);
  and and_2 (and_2_out, in, not_2_out);
  Clock clock_2 (.out(clock_2_out));
  Counter #(.width(16), .max('hffff)) counter_1 (
    .load(1'b0), .count(and_2_out), .Q(counter_1_q), .clk(clock_2_out), .clr(or_1_out));  // open: D, carry
  Equal equal_1 (.x(\time ), .y(counter_1_q), .out(done));
endmodule

module Timed_brain (
  input  in,
  output green,
  output amber,
  output red,
  output flash_amber
);

  wire and_1_out, or_1_out, timer_1_done, timer_2_done, timer_3_done;

  and and_1 (and_1_out, green, in);
  or or_1 (or_1_out, and_1_out, timer_1_done, timer_2_done, timer_3_done);
  Brain brain_1 (.change(or_1_out), .green(green), .amber(amber), .red(red), .flash_amber(flash_amber));
  Timer timer_1 (.\time (16'h400), .in(amber), .done(timer_1_done));
  Timer timer_2 (.\time (16'h1e00), .in(red), .done(timer_2_done));
  Timer timer_3 (.\time (16'ha00), .in(flash_amber), .done(timer_3_done));
endmodule

module Flash_generator (
  input  in,
  output out
);

  wire and_1_out, and_3_out, d_ff_1_q, d_ff_1_qn, not_1_out, or_1_out, timer_1_done, timer_2_done;

  and and_1 (and_1_out, in, d_ff_1_qn);
  Timer timer_1 (.\time (16'h199), .in(and_1_out), .done(timer_1_done));
  or or_1 (or_1_out, timer_1_done, timer_2_done);
  D_Flip_Flop d_ff_1 (
    .clk(or_1_out), .D(d_ff_1_qn), .Q(d_ff_1_q), .Qn(d_ff_1_qn), .reset(not_1_out));  // open: preset, en
  not not_1 (not_1_out, in);
  and and_2 (out, in, d_ff_1_qn);
  Timer timer_2 (.\time (16'h199), .in(and_3_out), .done(timer_2_done));
  and and_3 (and_3_out, in, d_ff_1_q);
endmodule

module Traffic_Light (
  input  inc
);

  wire flash_generator_1_out, or_1_out, timed_brain_1_amber, timed_brain_1_flash_amber, timed_brain_1_green,
       timed_brain_1_red;

  Timed_brain timed_brain_1 (
    .in(inc), .green(timed_brain_1_green), .amber(timed_brain_1_amber), .red(timed_brain_1_red),
    .flash_amber(timed_brain_1_flash_amber));
  Flash_generator flash_generator_1 (.in(timed_brain_1_flash_amber), .out(flash_generator_1_out));
  LED led_1 (.in(timed_brain_1_red));
  LED led_2 (.in(or_1_out));
  or or_1 (or_1_out, timed_brain_1_amber, flash_generator_1_out);
  LED led_3 (.in(timed_brain_1_green));
endmodule
