// Logisim project lab1.circ as structural Verilog
module exercise1 (
  input  A,
  input  C,
  input  B,
  output out_4,
  output out_5
);

  wire and_1_out, and_2_out, or_1_out, or_2_out;

  and and_1 (and_1_out, A, C);
  and and_2 (and_2_out, C, B);
  or or_1 (or_1_out, A, B);
  or or_2 (or_2_out, and_1_out, and_2_out);
  and and_3 (out_5, or_1_out, C);
  and and_4 (out_4, C, or_2_out);
endmodule

module exercise2 (
  input  B,
  input  A,
  input  C,
  output out_4,
  output out_5
);

  wire and_1_out, or_1_out, or_2_out;

  and and_1 (and_1_out, B, A);
  or or_1 (or_1_out, ~A, C);  // OR_Gate
  or or_2 (or_2_out, ~C, B);  // OR_Gate
  or or_3 (out_4, and_1_out, ~or_1_out);  // OR_Gate
  and and_2 (out_5, or_2_out, A);
endmodule

module exercise3 (
  input  A,
  input  B,
  input  C,
  output out_4,
  output out_5
);

  wire and_1_out, or_1_out;

  and and_1 (and_1_out, B, C);
  or or_1 (or_1_out, A, ~and_1_out);  // OR_Gate
  and and_2 (out_5, ~A, B, C);  // AND_Gate
  not not_1 (out_4, or_1_out);
endmodule

module exercise4 (
  input  A,
  input  C,
  input  B,
  output out_4,
  output out_5
);

  wire and_1_out, and_2_out, or_1_out;

  or or_1 (or_1_out, A, C);
  and and_1 (and_1_out, B, C);
  and and_2 (and_2_out, or_1_out, B);
  or or_2 (out_4, A, and_2_out);
  or or_3 (out_5, and_1_out, A);
endmodule

module exercise5 (
  input  A,
  input  in_2,
  input  C,
  output out_4,
  output out_5
);

  wire and_1_out, or_1_out, or_2_out;

  or or_1 (or_1_out, A, in_2);
  or or_2 (or_2_out, in_2, ~A);  // OR_Gate
  or or_3 (out_5, in_2, C);
  and and_1 (and_1_out, or_1_out, or_2_out);
  or or_4 (out_4, and_1_out, C);

  // Notes on the sheet:
  //   B
endmodule

module exercise6 (
  input  A,
  input  B,
  input  C,
  output out_4,
  output out_5
);

  wire and_1_out, and_2_out, and_3_out;

  and and_1 (and_1_out, A, B, C);
  and and_2 (and_2_out, A, B);
  and and_3 (and_3_out, ~and_1_out, C);  // AND_Gate
  or or_1 (out_5, and_2_out, ~C);  // OR_Gate
  not not_1 (out_4, and_3_out);
endmodule

module nand1 (
  input  in_1,
  output out_2
);

  wire and_1_out;

  not not_1 (out_2, and_1_out);
  and and_1 (and_1_out, in_1, in_1);
endmodule

module nand2 (
  input  in_1,
  input  in_2,
  output out_3
);

  wire and_1_out, and_2_out, not_1_out;

  and and_1 (and_1_out, in_1, in_2);
  not not_1 (not_1_out, and_1_out);
  not not_2 (out_3, and_2_out);
  and and_2 (and_2_out, not_1_out, not_1_out);
endmodule

module nand3 (
  input  in_1,
  input  in_2,
  output out_3
);

  wire and_1_out, and_2_out, and_3_out, not_1_out, not_2_out;

  and and_1 (and_1_out, in_1, in_1);
  and and_2 (and_2_out, in_2, in_2);
  not not_1 (not_1_out, and_1_out);
  not not_2 (not_2_out, and_2_out);
  and and_3 (and_3_out, not_1_out, not_2_out);
  not not_3 (out_3, and_3_out);
endmodule

module nand4 (
  input  in_1,
  input  in_2,
  output out_3
);

  wire and_1_out, and_2_out, and_3_out, and_4_out, not_1_out, not_2_out, not_3_out;

  and and_1 (and_1_out, in_1, in_1);
  and and_2 (and_2_out, in_2, in_2);
  not not_1 (not_1_out, and_1_out);
  not not_2 (not_2_out, and_2_out);
  and and_3 (and_3_out, not_1_out, not_2_out);
  not not_3 (not_3_out, and_3_out);
  not not_4 (out_3, and_4_out);
  and and_4 (and_4_out, not_3_out, not_3_out);
endmodule

module nand5 (
  input  in_1,
  input  in_2,
  output out_3,
  output out_4
);

  wire and_1_out, and_2_out, and_3_out, and_4_out, and_5_out, and_6_out, and_7_out, and_8_out, and_9_out,
       and_10_out, and_11_out, not_1_out, not_2_out, not_3_out, not_4_out, not_5_out, not_6_out, not_7_out,
       not_8_out, not_9_out;

  and and_1 (and_1_out, in_1, in_1);
  not not_1 (not_1_out, and_1_out);
  and and_2 (and_2_out, in_2, in_2);
  not not_2 (not_2_out, and_2_out);
  and and_3 (and_3_out, in_2, in_2);
  not not_3 (not_3_out, and_3_out);
  not not_4 (not_4_out, and_4_out);
  and and_4 (and_4_out, in_1, in_1);
  and and_5 (and_5_out, not_1_out, not_2_out);
  not not_5 (not_5_out, and_5_out);
  not not_6 (not_6_out, and_6_out);
  and and_6 (and_6_out, in_1, in_2);
  not not_7 (not_7_out, and_7_out);
  and and_7 (and_7_out, in_1, not_3_out);
  not not_8 (not_8_out, and_8_out);
  and and_8 (and_8_out, not_4_out, in_2);
  and and_9 (and_9_out, not_5_out, not_6_out);
  not not_9 (not_9_out, and_9_out);
  and and_10 (and_10_out, not_7_out, not_8_out);
  and and_11 (and_11_out, not_9_out, not_9_out);
  not not_10 (out_3, and_10_out);
  not not_11 (out_4, and_11_out);
endmodule

module variable_5 (
  input  in_1,
  input  in_2,
  input  in_3,
  input  in_4,
  input  in_5,
  output out_6
);

  wire and_1_out, and_2_out, and_3_out, and_4_out, not_1_out, not_2_out, not_3_out, not_4_out, or_1_out;

  not not_1 (not_1_out, in_1);
  not not_2 (not_2_out, in_3);
  not not_3 (not_3_out, in_5);
  and and_1 (and_1_out, in_2, not_2_out);
  or or_1 (or_1_out, not_1_out, and_1_out);
  not not_4 (not_4_out, in_4);
  and and_2 (and_2_out, or_1_out, in_4);
  and and_3 (and_3_out, in_3, not_4_out);
  or or_2 (out_6, and_2_out, and_4_out);
  and and_4 (and_4_out, and_3_out, not_3_out);
endmodule

module variable_5_nand (
  input  in_1,
  input  in_2,
  input  in_3,
  input  in_4,
  input  in_5,
  output out_6
);

  wire _1_out, _2_out, _3_out, _4_out, _5_out, _6_out, _7_out, _8_out, _9_out, _10_out, not_1_out, not_2_out,
       not_3_out, not_4_out, not_5_out, not_6_out, not_7_out, not_8_out, not_9_out;

  and _3 (_3_out, in_3, in_3);
  not not_1 (not_1_out, _3_out);
  and _4 (_4_out, in_4, in_4);
  and _9 (_9_out, in_5, in_5);
  and _2 (_2_out, in_2, not_1_out);
  not not_2 (not_2_out, _4_out);
  not not_3 (not_3_out, _9_out);
  and _1 (_1_out, in_1, not_4_out);
  not not_4 (not_4_out, _2_out);
  and _6 (_6_out, in_3, not_2_out);
  not not_5 (not_5_out, _1_out);
  not not_6 (not_6_out, _6_out);
  and _7 (_7_out, not_6_out, not_6_out);
  and _5 (_5_out, not_5_out, in_4);
  not not_7 (not_7_out, _5_out);
  not not_8 (not_8_out, _7_out);
  and _10 (_10_out, not_8_out, not_3_out);
  not not_9 (not_9_out, _10_out);
  and _8 (_8_out, not_7_out, not_9_out);
  not not_10 (out_6, _8_out);
endmodule
