// Logisim project lab2.circ as structural Verilog
module half_adder_comp (
  input  A,
  input  B,
  output C,
  output S
);

  and and_1 (C, A, B);
  xor xor_1 (S, A, B);
endmodule

module full_adder_comp (
  input  Cin,
  input  A,
  input  B,
  output S,
  output C_out
);

  wire and_1_out, and_2_out, and_3_out, or_1_out, xor_1_out;

  xor xor_1 (xor_1_out, Cin, A);
  and and_1 (and_1_out, Cin, A);
  and and_2 (and_2_out, Cin, B);
  and and_3 (and_3_out, A, B);
  xor xor_2 (S, xor_1_out, B);
  or or_1 (or_1_out, and_1_out, and_2_out);
  or or_2 (C_out, or_1_out, and_3_out);
endmodule

module full_adder_4 (
  input  [3:0] A,
  input  [3:0] B,
  output [3:0] S,
  output C
);

  wire full_adder_comp_1_c_out, full_adder_comp_2_c_out, full_adder_comp_3_c_out;

  full_adder_comp full_adder_comp_1 (.Cin(1'b0), .A(A[0]), .B(B[0]), .S(S[0]), .C_out(full_adder_comp_1_c_out));
  full_adder_comp full_adder_comp_2 (
    .Cin(full_adder_comp_1_c_out), .A(A[1]), .B(B[1]), .S(S[1]), .C_out(full_adder_comp_2_c_out));
  full_adder_comp full_adder_comp_3 (
    .Cin(full_adder_comp_2_c_out), .A(A[2]), .B(B[2]), .S(S[2]), .C_out(full_adder_comp_3_c_out));
  full_adder_comp full_adder_comp_4 (.Cin(full_adder_comp_3_c_out), .A(A[3]), .B(B[3]), .S(S[3]), .C_out(C));
endmodule

module incrementer (
  input  [3:0] A,
  output [3:0] S,
  output C
);

  wire half_adder_comp_1_c, half_adder_comp_2_c, half_adder_comp_3_c;

  half_adder_comp half_adder_comp_1 (.A(1'b1), .B(A[0]), .C(half_adder_comp_1_c), .S(S[0]));
  half_adder_comp half_adder_comp_2 (.A(half_adder_comp_1_c), .B(A[1]), .C(half_adder_comp_2_c), .S(S[1]));
  half_adder_comp half_adder_comp_3 (.A(half_adder_comp_2_c), .B(A[2]), .C(half_adder_comp_3_c), .S(S[2]));
  half_adder_comp half_adder_comp_4 (.A(half_adder_comp_3_c), .B(A[3]), .C(C), .S(S[3]));
endmodule

module adder_and_subtracter (
  input  [3:0] A,
  input  _0A1S,
  input  [3:0] B,
  output [3:0] S,
  output C
);

  wire full_adder_comp_1_c_out, full_adder_comp_2_c_out, full_adder_comp_3_c_out;
  wire [3:0] incrementer_1_s, multiplexer_1_out, not_1_out;

  not not_1 (not_1_out[0], B[0]);
  not not_2 (not_1_out[1], B[1]);
  not not_3 (not_1_out[2], B[2]);
  not not_4 (not_1_out[3], B[3]);
  incrementer incrementer_1 (.A(not_1_out), .S(incrementer_1_s));  // open: C
  Multiplexer #(.width(4), .enable("false")) multiplexer_1 (
    .in0(B), .in1(incrementer_1_s), .out(multiplexer_1_out), .sel(_0A1S));
  full_adder_comp full_adder_comp_1 (
    .Cin(1'b0), .A(A[0]), .B(multiplexer_1_out[0]), .S(S[0]), .C_out(full_adder_comp_1_c_out));
  full_adder_comp full_adder_comp_2 (
    .Cin(full_adder_comp_1_c_out), .A(A[1]), .B(multiplexer_1_out[1]), .S(S[1]),
    .C_out(full_adder_comp_2_c_out));
  full_adder_comp full_adder_comp_3 (
    .Cin(full_adder_comp_2_c_out), .A(A[2]), .B(multiplexer_1_out[2]), .S(S[2]),
    .C_out(full_adder_comp_3_c_out));
  full_adder_comp full_adder_comp_4 (
    .Cin(full_adder_comp_3_c_out), .A(A[3]), .B(multiplexer_1_out[3]), .S(S[3]), .C_out(C));
endmodule

module NAND_half_adder (
  input  A,
  input  B,
  output C,
  output S
);

  wire and_1_out, and_2_out, and_3_out, and_4_out, and_5_out, not_1_out, not_2_out, not_3_out;

  and and_1 (and_1_out, A, B);
  not not_1 (not_1_out, and_1_out);
  and and_2 (and_2_out, A, not_1_out);
  and and_3 (and_3_out, not_1_out, B);
  not not_2 (not_2_out, and_2_out);
  not not_3 (not_3_out, and_3_out);
  and and_4 (and_4_out, not_1_out, not_1_out);
  and and_5 (and_5_out, not_2_out, not_3_out);
  not not_4 (C, and_4_out);
  not not_5 (S, and_5_out);
endmodule

module NAND_full_adder (
  input  Cin,
  input  A,
  input  B,
  output S,
  output C_out
);

  wire nand_1_out, nand_2_out, nand_3_out, nand_4_out, nand_5_out, nand_6_out, nand_7_out, nand_8_out,
       nand_9_out, nand_11_out, nand_12_out;

  nand nand_1 (nand_1_out, Cin, A);
  nand nand_2 (nand_2_out, Cin, B);
  nand nand_3 (nand_3_out, A, B);
  nand nand_4 (nand_4_out, Cin, nand_1_out);
  nand nand_5 (nand_5_out, nand_1_out, A);
  nand nand_6 (nand_6_out, nand_1_out, nand_2_out);
  nand nand_7 (nand_7_out, nand_4_out, nand_5_out);
  nand nand_8 (nand_8_out, nand_6_out, nand_6_out);
  nand nand_9 (nand_9_out, nand_7_out, B);
  nand nand_10 (C_out, nand_8_out, nand_3_out);
  nand nand_11 (nand_11_out, nand_7_out, nand_9_out);
  nand nand_12 (nand_12_out, nand_9_out, B);
  nand nand_13 (S, nand_11_out, nand_12_out);
endmodule

module NAND_incrementer_3bit (
  input  [2:0] A,
  output [2:0] S,
  output C
);

  wire and_1_out, and_2_out, and_3_out, and_4_out, and_5_out, and_6_out, and_7_out, and_8_out, and_9_out,
       and_10_out, and_11_out, and_12_out, and_13_out, and_14_out, and_15_out, not_1_out, not_2_out,
       not_3_out, not_4_out, not_5_out, not_6_out, not_7_out, not_8_out, not_9_out, not_10_out, not_12_out;

  and and_1 (and_1_out, 1'b1, A[0]);
  and and_2 (and_2_out, not_10_out, A[1]);
  and and_3 (and_3_out, not_12_out, A[2]);
  not not_1 (not_1_out, and_1_out);
  not not_2 (not_2_out, and_2_out);
  not not_3 (not_3_out, and_3_out);
  and and_4 (and_4_out, 1'b1, not_1_out);
  and and_5 (and_5_out, not_1_out, A[0]);
  and and_6 (and_6_out, not_10_out, not_2_out);
  and and_7 (and_7_out, not_2_out, A[1]);
  and and_8 (and_8_out, not_12_out, not_3_out);
  and and_9 (and_9_out, not_3_out, A[2]);
  not not_4 (not_4_out, and_4_out);
  not not_5 (not_5_out, and_5_out);
  not not_6 (not_6_out, and_6_out);
  not not_7 (not_7_out, and_7_out);
  not not_8 (not_8_out, and_8_out);
  not not_9 (not_9_out, and_9_out);
  and and_10 (and_10_out, not_1_out, not_1_out);
  and and_11 (and_11_out, not_4_out, not_5_out);
  and and_12 (and_12_out, not_2_out, not_2_out);
  and and_13 (and_13_out, not_6_out, not_7_out);
  and and_14 (and_14_out, not_3_out, not_3_out);
  and and_15 (and_15_out, not_8_out, not_9_out);
  not not_10 (not_10_out, and_10_out);
  not not_11 (S[0], and_11_out);
  not not_12 (not_12_out, and_12_out);
  not not_13 (S[1], and_13_out);
  not not_14 (S[2], and_14_out);
  not not_15 (C, and_15_out);
endmodule

module Plexers (
  input  in_1,
  input  in_2,
  input  [3:0] A,
  input  [1:0] in_4,
  input  [3:0] B,
  output [3:0] out_6
);

  wire demultiplexer_1_out1;
  wire [3:0] and_1_out, nor_1_out, or_1_out, xor_1_out;

  and and_1 (and_1_out[0], A[0], B[0]);
  and and_2 (and_1_out[1], A[1], B[1]);
  and and_3 (and_1_out[2], A[2], B[2]);
  and and_4 (and_1_out[3], A[3], B[3]);
  or or_1 (or_1_out[0], A[0], B[0]);
  or or_2 (or_1_out[1], A[1], B[1]);
  or or_3 (or_1_out[2], A[2], B[2]);
  or or_4 (or_1_out[3], A[3], B[3]);
  xor xor_1 (xor_1_out[0], A[0], B[0]);
  xor xor_2 (xor_1_out[1], A[1], B[1]);
  xor xor_3 (xor_1_out[2], A[2], B[2]);
  xor xor_4 (xor_1_out[3], A[3], B[3]);
  nor nor_1 (nor_1_out[0], A[0], B[0]);
  nor nor_2 (nor_1_out[1], A[1], B[1]);
  nor nor_3 (nor_1_out[2], A[2], B[2]);
  nor nor_4 (nor_1_out[3], A[3], B[3]);
  Demultiplexer #(.enable("false")) demultiplexer_1 (.out1(demultiplexer_1_out1), .in(in_2), .sel(in_1));  // open: out0
  Multiplexer #(.select(2), .width(4)) multiplexer_1 (
    .in0(and_1_out), .in1(or_1_out), .in2(xor_1_out), .in3(nor_1_out), .out(out_6), .sel(in_4),
    .en(demultiplexer_1_out1));
endmodule

module HACK_ALU (
  input  zx,
  input  nx,
  input  [3:0] x,
  input  f,
  input  n,
  input  zy,
  input  ny,
  input  [3:0] y,
  output [3:0] out_9
);

  wire [3:0] and_1_out, full_adder_4_1_s, multiplexer_1_out, multiplexer_2_out, multiplexer_3_out,
       multiplexer_4_out, multiplexer_5_out, not_1_out, not_2_out, not_3_out;

  Multiplexer #(.width(4), .enable("false")) multiplexer_1 (.in0(x), .in1(4'b0000), .out(multiplexer_1_out), .sel(zx));
  Multiplexer #(.width(4), .enable("false")) multiplexer_2 (.in0(y), .in1(4'b0000), .out(multiplexer_2_out), .sel(zy));
  assign not_1_out = ~multiplexer_1_out;  // NOT_Gate not_1, 4 bits wide
  assign not_2_out = ~multiplexer_2_out;  // NOT_Gate not_2, 4 bits wide
  Multiplexer #(.width(4), .enable("false")) multiplexer_3 (
    .in0(multiplexer_1_out), .in1(not_1_out), .out(multiplexer_3_out), .sel(nx));
  Multiplexer #(.width(4), .enable("false")) multiplexer_4 (
    .in0(multiplexer_2_out), .in1(not_2_out), .out(multiplexer_4_out), .sel(ny));
  assign and_1_out = multiplexer_3_out & multiplexer_4_out;  // AND_Gate and_1, 4 bits wide
  full_adder_4 full_adder_4_1 (.A(multiplexer_3_out), .B(multiplexer_4_out), .S(full_adder_4_1_s));  // open: C
  Multiplexer #(.width(4), .enable("false")) multiplexer_5 (
    .in0(and_1_out), .in1(full_adder_4_1_s), .out(multiplexer_5_out), .sel(f));
  Multiplexer #(.width(4), .enable("false")) multiplexer_6 (
    .in0(multiplexer_5_out), .in1(not_3_out), .out(out_9), .sel(n));
  assign not_3_out = ~multiplexer_5_out;  // NOT_Gate not_3, 4 bits wide
endmodule
